// Logisim project Logisim Logic PCB State Machine Simulation.circ as structural Verilog: 1 circuit, main circuit main
module main (
);

  wire and_1_out, and_2_out, and_3_out, and_4_out, and_5_out, and_6_out, and_7_out, and_8_out, and_9_out,
       and_10_out, and_11_out, and_12_out, clock_1_out, multiplexer_1_out, multiplexer_2_out,
       multiplexer_3_out, multiplexer_4_out, multiplexer_5_out, multiplexer_6_out, multiplexer_7_out,
       multiplexer_8_out, multiplexer_9_out, not_1_out, not_2_out, not_3_out, or_1_out, or_2_out, or_3_out,
       or_4_out, or_5_out, or_6_out;
  wire [2:0] t_ff_3_q;

  Clock clock_1 (.out(clock_1_out));
  and and_1 (and_1_out, not_1_out, t_ff_3_q[1], t_ff_3_q[0]);
  and and_2 (and_2_out, t_ff_3_q[2], not_2_out, t_ff_3_q[0]);
  or or_1 (or_1_out, and_1_out, and_2_out);
  and and_3 (and_3_out, not_1_out, t_ff_3_q[0]);
  T_Flip_Flop t_ff_1 (.clk(clock_1_out), .T(or_1_out), .Q(t_ff_3_q[2]));  // open: Qn, preset, reset, en
  not not_1 (not_1_out, t_ff_3_q[2]);
  T_Flip_Flop t_ff_2 (.clk(clock_1_out), .T(and_3_out), .Q(t_ff_3_q[1]));  // open: Qn, preset, reset, en
  T_Flip_Flop t_ff_3 (.clk(clock_1_out), .T(1'b1), .Q(t_ff_3_q[0]));  // open: Qn, preset, reset, en
  not not_2 (not_2_out, t_ff_3_q[1]);
  not not_3 (not_3_out, t_ff_3_q[0]);
  Multiplexer #(.select(3), .enable("false")) multiplexer_1 (
    .in0(1'b1), .in1(1'b1), .in2(1'b0), .in3(1'b1), .in4(1'b1), .in5(1'b0), .out(multiplexer_1_out),
    .sel(t_ff_3_q));  // open: in6, in7
  Multiplexer #(.select(3), .enable("false")) multiplexer_2 (
    .in0(1'b0), .in1(1'b0), .in2(1'b1), .in3(1'b0), .in4(1'b0), .in5(1'b0), .out(multiplexer_2_out),
    .sel(t_ff_3_q));  // open: in6, in7
  Multiplexer #(.select(3), .enable("false")) multiplexer_3 (
    .in0(1'b1), .in1(1'b0), .in2(1'b1), .in3(1'b0), .in4(1'b0), .in5(1'b0), .out(multiplexer_3_out),
    .sel(t_ff_3_q));  // open: in6, in7
  Multiplexer #(.select(3), .enable("false")) multiplexer_4 (
    .in0(1'b1), .in1(1'b1), .in2(1'b0), .in3(1'b0), .in4(1'b1), .in5(1'b0), .out(multiplexer_4_out),
    .sel(t_ff_3_q));  // open: in6, in7
  Multiplexer #(.select(3), .enable("false")) multiplexer_5 (
    .in0(1'b1), .in1(1'b1), .in2(1'b1), .in3(1'b0), .in4(1'b1), .in5(1'b0), .out(multiplexer_5_out),
    .sel(t_ff_3_q));  // open: in6, in7
  Multiplexer #(.select(3), .enable("false")) multiplexer_6 (
    .in0(1'b0), .in1(1'b0), .in2(1'b1), .in3(1'b0), .in4(1'b0), .in5(1'b1), .out(multiplexer_6_out),
    .sel(t_ff_3_q));  // open: in6, in7
  Multiplexer #(.select(3), .enable("false")) multiplexer_7 (
    .in0(1'b0), .in1(1'b0), .in2(1'b0), .in3(1'b1), .in4(1'b0), .in5(1'b0), .out(multiplexer_7_out),
    .sel(t_ff_3_q));  // open: in6, in7
  Multiplexer #(.select(3), .enable("false")) multiplexer_8 (
    .in0(1'b0), .in1(1'b0), .in2(1'b0), .in3(1'b0), .in4(1'b0), .in5(1'b1), .out(multiplexer_8_out),
    .sel(t_ff_3_q));  // open: in6, in7
  Multiplexer #(.select(3), .enable("false")) multiplexer_9 (
    .in0(1'b0), .in1(1'b1), .in2(1'b0), .in3(1'b0), .in4(1'b1), .in5(1'b0), .out(multiplexer_9_out),
    .sel(t_ff_3_q));  // open: in6, in7
  and and_4 (and_4_out, not_1_out, t_ff_3_q[0]);
  and and_5 (and_5_out, not_2_out, not_3_out);
  and and_6 (and_6_out, not_1_out, t_ff_3_q[1], not_3_out);
  and and_7 (and_7_out, not_1_out, not_3_out);
  and and_8 (and_8_out, not_1_out, not_2_out);
  and and_9 (and_9_out, t_ff_3_q[2], not_2_out, t_ff_3_q[0]);
  and and_10 (and_10_out, not_1_out, t_ff_3_q[1], t_ff_3_q[0]);
  and and_11 (and_11_out, not_1_out, not_2_out, t_ff_3_q[0]);
  and and_12 (and_12_out, t_ff_3_q[2], not_2_out, not_3_out);
  or or_2 (or_2_out, and_11_out, and_12_out);
  or or_3 (or_3_out, and_4_out, and_5_out);
  or or_4 (or_4_out, and_8_out, and_5_out);
  or or_5 (or_5_out, and_5_out, and_8_out, and_7_out);
  or or_6 (or_6_out, and_6_out, and_9_out);
  LED led_1 (.in(multiplexer_5_out));
  LED led_2 (.in(multiplexer_5_out));
  LED led_3 (.in(multiplexer_1_out));
  LED led_4 (.in(multiplexer_6_out));
  LED led_5 (.in(multiplexer_7_out));
  LED led_6 (.in(multiplexer_9_out));
  LED led_7 (.in(multiplexer_8_out));
  LED led_8 (.in(multiplexer_7_out));
  LED led_9 (.in(multiplexer_4_out));
  LED led_10 (.in(multiplexer_1_out));
  LED led_11 (.in(multiplexer_8_out));
  LED led_12 (.in(multiplexer_2_out));
  LED led_13 (.in(multiplexer_4_out));
  LED led_14 (.in(multiplexer_6_out));
  LED led_15 (.in(multiplexer_3_out));
  LED led_16 (.in(multiplexer_4_out));
  LED led_17 (.in(or_3_out));
  LED led_18 (.in(or_5_out));
  LED led_19 (.in(and_10_out));
  LED led_20 (.in(or_6_out));
  LED led_21 (.in(or_2_out));
  LED led_22 (.in(and_9_out));
  LED led_23 (.in(or_5_out));
  LED led_24 (.in(and_10_out));
  LED led_25 (.in(or_4_out));
  LED led_26 (.in(or_3_out));
  LED led_27 (.in(and_6_out));
  LED led_28 (.in(and_9_out));
  LED led_29 (.in(or_4_out));
  LED led_30 (.in(or_6_out));
  LED led_31 (.in(and_7_out));
  LED led_32 (.in(or_4_out));
endmodule
